# Fritzing sketch MacroXiao (saved by Fritzing 0.9.6b)
circuit board: 8.507cm x 5.19403cm
breadboards: 1

parts:
  BUTTON1 = Arcade Button (white)
  BUTTON2 = Arcade Button (green)
  BUTTON3 = Arcade Button (yellow)
  Mod1 = seeeduino-xiao
  R2 = Resistor [tolerance=±5% power=0.25 resistance=10k package=THT]
  R3 = Resistor [tolerance=±5% power=0.25 resistance=10k package=THT]
  LED1 = LED - 5mm [color="White (4500K)" current=0.030 package="5 mm [THT]"]
  LED2 = LED - 5mm [color="Green (570nm)" current=0.030 package="5 mm [THT]"]
  LED3 = LED - 5mm [color="Yellow (595nm)" current=0.030 package="5 mm [THT]"]
  NEOPIXEL1 = Neopixel Strip -- Black (30/m)
  R1 = Resistor [tolerance=±5% power=0.25 resistance=10k package=THT]

nets:
  N1: BUTTON1.no_name_yet#1, Mod1.D6, R1.Pin_0
  5V: BUTTON1.no_name_yet#2, BUTTON2.no_name_yet#2, BUTTON3.no_name_yet#2, Mod1.5V, LED1.anode, LED2.anode, LED3.anode, NEOPIXEL1.+5V
  N2: BUTTON2.no_name_yet#1, Mod1.D5, R2.Pin_0
  N3: BUTTON3.no_name_yet#1, Mod1.D4, R3.Pin_0
  N4: Mod1.D3, NEOPIXEL1.Din
  GND: Mod1.GND, R2.Pin_1, R3.Pin_1, LED1.cathode, LED2.cathode, LED3.cathode, NEOPIXEL1.GND, R1.Pin_1

notes:
  These LEDs are inside the buttons and have built in resistors

custom parts:
  Arcade Button (white): Adafruit Arcade Button (white)
  Arcade Button (green): Adafruit Arcade Button (green)
  Arcade Button (yellow): Adafruit Arcade Button (yellow)
  seeeduino-xiao: Seeeduino XIAO processor board.
  Neopixel Strip -- Black (30/m): These NeoPixel strips have 30 digitally-addressable pixel LEDs per meter and are very affordable and are only 12.5 mm wide, 10 mm if you remove the strip from the casing.
